# Fritzing sketch Circuito (saved by Fritzing 0.9.3b)
breadboards: 1

parts:
  Componente1 = LCD1602-I2C
  S1 = Round Pushbutton
  S2 = Round Pushbutton
  S3 = Round Pushbutton
  S4 = Round Pushbutton
  JACK1 = 2.1mm Barrel Jack with Terminal Block
  Part3 = Coin Acceptor - 6-Coin version
  Componente3 = Arduino Mega 2560 (Rev3)
  Matrix_keypad2 = KEYPAD 4x4
  S5 = Square Pushbutton
  J5 = Basic Servo
  J6 = Basic Servo
  J7 = Basic Servo
  J8 = Basic Servo
  J9 = Basic Servo

nets:
  GND: Componente1.GND, S1.leg1, S2.leg1, S3.leg1, S4.leg1, JACK1.NEG, Part3.GND, Componente3.GND, S5.leg1, J5.gnd, J6.gnd, J7.gnd, J8.gnd, J9.gnd
  VCC: Componente1.VCC, Componente3.5V, J5.vcc, J6.vcc, J7.vcc, J8.vcc, J9.vcc
  N1: Componente1.SDA, Componente3.D20/SDA
  N2: Componente1.SCL, Componente3.D21/SCL
  N3: S1.leg0, Componente3.D10_PWM
  N4: S2.leg0, Componente3.D11_PWM
  N5: S3.leg0, Componente3.D8_PWM
  N6: S4.leg0, Componente3.D9_PWM
  N7: JACK1.POS, Part3.12V
  N8: Part3.SIG, Componente3.D2_PWM
  N9: Componente3.D12_PWM, S5.leg0
  N10: Componente3.D3_PWM, J6.pulse
  N11: Componente3.D4_PWM, J7.pulse
  N12: Componente3.D5_PWM, J8.pulse
  N13: Componente3.D6_PWM, J5.pulse
  N14: Componente3.D7_PWM, J9.pulse
  N15: Componente3.D39, Matrix_keypad2.col1
  N16: Componente3.D41, Matrix_keypad2.col2
  N17: Componente3.D43, Matrix_keypad2.col3
  N18: Componente3.D45, Matrix_keypad2.col4
  N19: Componente3.D47, Matrix_keypad2.row1
  N20: Componente3.D49, Matrix_keypad2.row2
  N21: Componente3.D51, Matrix_keypad2.row3
  N22: Componente3.D53, Matrix_keypad2.row4

custom parts:
  LCD1602-I2C: A standard character display, usually with 2x16 characters. Comes in many colors with LCM1602 IIC attached.
  Coin Acceptor - 6-Coin version: 12V coin acceptor that can handle up to 6 different denominations. Output is either pulse width, serial, or single pin per coin value.
  KEYPAD 4x4: Matrix keypad 16 buttons, 4 rows x 4 columns
