# Fritzing sketch Circuito (saved by Fritzing 0.9.3b)
breadboards: 1

parts:
  Componente1 = Arduino Mega 2560 (Rev3)
  J1 = Basic Servo
  S2 = Round Pushbutton

nets:
  N1: Componente1.D10_PWM, J1.pulse
  N2: Componente1.D8_PWM, S2.leg0
  5V: Componente1.5V, J1.vcc
  GND: Componente1.GND, J1.gnd, S2.leg1
