# Fritzing sketch Circuito (saved by Fritzing 0.9.3b)
breadboards: 1

parts:
  Componente1 = Arduino Mega 2560 (Rev3)
  Part5 = Coin Acceptor - 6-Coin version
  JACK3 = 2.1mm Barrel Jack with Terminal Block

nets:
  GND: Componente1.GND, Part5.GND, JACK3.NEG
  N1: Componente1.D2_PWM, Part5.SIG
  N2: Part5.12V, JACK3.POS

custom parts:
  Coin Acceptor - 6-Coin version: 12V coin acceptor that can handle up to 6 different denominations. Output is either pulse width, serial, or single pin per coin value.
