# Fritzing sketch Circuito (saved by Fritzing 0.9.3b)
breadboards: 1

parts:
  Componente1 = Arduino Mega 2560 (Rev3)
  M1 = fc-51 [package=THT]
  J1 = Basic Servo

nets:
  N1: Componente1.D10_PWM, J1.pulse
  N2: Componente1.D8_PWM, M1.pin1
  5V: Componente1.5V, M1.pin3, J1.vcc
  GND: Componente1.GND, M1.pin2, J1.gnd
