# Fritzing sketch Circuito (saved by Fritzing 0.9.3b)

parts:
  Componente1 = Arduino Mega 2560 (Rev3)
  Matrix_keypad3 = KEYPAD 4x4

nets:
  N1: Componente1.D39, Matrix_keypad3.col1
  N2: Componente1.D41, Matrix_keypad3.col2
  N3: Componente1.D43, Matrix_keypad3.col3
  N4: Componente1.D45, Matrix_keypad3.col4
  N5: Componente1.D47, Matrix_keypad3.row1
  N6: Componente1.D49, Matrix_keypad3.row2
  N7: Componente1.D51, Matrix_keypad3.row3
  N8: Componente1.D53, Matrix_keypad3.row4

custom parts:
  KEYPAD 4x4: Matrix keypad 16 buttons, 4 rows x 4 columns
